# Fritzing sketch schema (saved by Fritzing 0.9.3b)
circuit board: 7.58648cm x 6.62665cm
breadboards: 1

parts:
  Composant1 = Arduino Nano (Rev3.0) (ICSP)
  AS3935 = rounded female pin header, 11 pins [form="♀ (female rounded)"]
  OLED = female pin header, 4 pins [form="♀ (female)"]
  ENCODER1 = Rotary Encoder with Knob
  C1 = Electrolytic Capacitor [capacitance=100nF package="100 mil [THT, electrolytic]"]
  C2 = Electrolytic Capacitor [capacitance=100nF package="100 mil [THT, electrolytic]"]
  C3 = Electrolytic Capacitor [capacitance=100nF package="100 mil [THT, electrolytic]"]
  piezzo = female pin header, 2 pins [form="♀ (female)"]
  Alim = female pin header, 2 pins [form="♀ (female)"]

nets:
  GND: Composant1.GND, AS3935.pin1, AS3935.pin2, AS3935.pin5, AS3935.pin10, OLED.pin1, ENCODER1.no_name_yet#2, ENCODER1.no_name_yet#4, C1.-, C2.-, C3.-, piezzo.pin1, Alim.pin2
  Rotation: Composant1.D2, ENCODER1.no_name_yet#1, C1.+
  IRQ: Composant1.D3, AS3935.pin4
  click: Composant1.D4, ENCODER1.no_name_yet#5, C3.+
  DIR: Composant1.D5, ENCODER1.no_name_yet#3, C2.+
  N1: Composant1.D7, piezzo.pin2
  CS: Composant1.D10, AS3935.pin6
  MOSI: Composant1.D11/MOSI, AS3935.pin8
  MISO: Composant1.D12/MISO, AS3935.pin7
  N2: Composant1.VIN, Alim.pin1
  5V: Composant1.5V, AS3935.pin3, AS3935.pin11, OLED.pin2
  N3: Composant1.A5, OLED.pin3
  N4: Composant1.A4, OLED.pin4
  SCK: Composant1.D13/SCK, AS3935.pin9

custom parts:
  Rotary Encoder with Knob: Rotary Encoder with 1/4" Shaft and Knob
